# Fritzing sketch AnalogInOut_Arduino_example (saved by Fritzing 0.8.7b)
breadboards: 1

parts:
  R1 = Resistor [package="2010 [SMD]"]  # not connected
  Part1 = Arduino Uno (Rev3)
  R2 = Rotary Potentiometer (Large) [maximum_resistance=100kΩ package=THT]  # not connected
  LED1 = LED - 5mm [color="Red (633nm)" package="5 mm [THT]"]
  R3 = Resistor [tolerance=±5% resistance=220 package=THT]

nets:
  N1: Part1.D9_PWM, R3.Pin_1
  N2: Part1.GND, LED1.cathode
  N3: LED1.anode, R3.Pin_0
