# Fritzing sketch Blink_Wave (saved by Fritzing 0.8.7b)
breadboards: 1

parts:
  Part1 = Arduino Uno (Rev3)
  LED1 = LED - 5mm [color="Red (633nm)" package="5 mm [THT]"]
  LED3 = LED - 5mm [color="Red (633nm)" package="5 mm [THT]"]
  LED4 = LED - 5mm [color="Red (633nm)" package="5 mm [THT]"]
  LED5 = LED - 5mm [color="Red (633nm)" package="5 mm [THT]"]
  LED6 = LED - 5mm [color="Red (633nm)" package="5 mm [THT]"]
  R1 = Resistor [tolerance=±5% resistance=220 package=THT]
  LED2 = LED - 5mm [color="Red (633nm)" package="5 mm [THT]"]
  R2 = Resistor [tolerance=±5% resistance=220 package=THT]
  R3 = Resistor [tolerance=±5% resistance=220 package=THT]
  R4 = Resistor [tolerance=±5% resistance=220 package=THT]
  R5 = Resistor [tolerance=±5% resistance=220 package=THT]
  R6 = Resistor [tolerance=±5% resistance=220 package=THT]

nets:
  N1: Part1.D8, R6.Pin_1
  N2: Part1.D9_PWM, R5.Pin_1
  N3: Part1.D10_PWM/SS, R4.Pin_1
  N4: Part1.D11_PWM/MOSI, R3.Pin_1
  N5: Part1.D12/MISO, R2.Pin_1
  N6: Part1.D13/SCK, R1.Pin_1
  N7: Part1.GND, LED1.cathode, LED3.cathode, LED4.cathode, LED5.cathode, LED6.cathode, LED2.cathode
  N8: LED1.anode, R2.Pin_0
  N9: LED3.anode, R4.Pin_0
  N10: LED4.anode, R6.Pin_0
  N11: LED5.anode, R1.Pin_0
  N12: LED6.anode, R5.Pin_0
  N13: LED2.anode, R3.Pin_0
