# Fritzing sketch Breathing_3LEDs (saved by Fritzing 0.8.7b)
breadboards: 1

parts:
  Part1 = Arduino Uno (Rev3)
  LED6 = LED - 5mm [color="Red (633nm)" package="5 mm [THT]"]
  R5 = Resistor [tolerance=±5% resistance=220 package=THT]
  LED8 = LED - 5mm [color="Green (570nm)" package="5 mm [THT]"]
  LED7 = LED - 5mm [color="Yellow (595nm)" package="5 mm [THT]"]
  R6 = Resistor [tolerance=±5% resistance=220 package=THT]
  R7 = Resistor [tolerance=±5% resistance=220 package=THT]

nets:
  N1: Part1.D9_PWM, R5.Pin_1
  N2: Part1.D10_PWM/SS, R6.Pin_1
  N3: Part1.D11_PWM/MOSI, R7.Pin_1
  N4: Part1.GND, LED6.cathode, LED8.cathode, LED7.cathode
  N5: LED6.anode, R5.Pin_0
  N6: LED8.anode, R7.Pin_0
  N7: LED7.anode, R6.Pin_0
