# Fritzing sketch Breathing_LED (saved by Fritzing 0.8.7b)
breadboards: 1

parts:
  Part1 = Arduino Uno (Rev3)
  LED6 = LED - 5mm [color="Red (633nm)" package="5 mm [THT]"]
  R5 = Resistor [tolerance=±5% resistance=220 package=THT]

nets:
  N1: Part1.D9_PWM, R5.Pin_1
  N2: Part1.GND, LED6.cathode
  N3: LED6.anode, R5.Pin_0
