# Fritzing sketch Button_Arduino_example (saved by Fritzing 0.8.7b)
breadboards: 1

parts:
  Part1 = Arduino Uno (Rev3)
  S3 = Pushbutton [package="[THT]"]
  LED1 = LED - 5mm [color="Red (633nm)" package="5 mm [THT]"]
  R1 = Resistor [tolerance=±5% resistance=220 package=THT]
  R2 = Resistor [tolerance=±5% resistance=10k package=THT]

nets:
  N1: Part1.D13/SCK, R1.Pin_1
  N2: Part1.D2, S3.Pin_1, S3.Pin_2, R2.Pin_0
  N3: Part1.5V, S3.Pin_3, S3.Pin_4
  N4: Part1.GND, R2.Pin_1
  N5: LED1.anode, R1.Pin_0
