# Fritzing sketch ColorMixingLamp_Arduino_example (saved by Fritzing 0.8.7b)
circuit board: 6.88566cm x 5.36311cm
breadboards: 1

parts:
  R4 = Resistor [resistance=220 tolerance=±5% package=THT]
  R5 = Resistor [resistance=220 tolerance=±5% package=THT]
  R6 = Resistor [resistance=220 tolerance=±5% package=THT]
  LED = RGB LED (com. cathode, rgb) [package="5 mm [THT]"]
  Arduino1 = Arduino Uno (Rev3)
  R7 = Photocell (LDR) [package=THT]
  R8 = Resistor [tolerance=±5% resistance=10k package=THT]
  R9 = Resistor [tolerance=±5% resistance=10k package=THT]
  R10 = Resistor [tolerance=±5% resistance=10k package=THT]
  R11 = Photocell (LDR) [package=THT]
  R12 = Photocell (LDR) [package=THT]

nets:
  N1: R4.Pin_0, Arduino1.D11_PWM/MOSI
  N2: R4.Pin_1, LED.red_anode
  N3: R5.Pin_0, Arduino1.D9_PWM
  N4: R5.Pin_1, LED.blue_anode
  N5: R6.Pin_0, Arduino1.D10_PWM/SS
  N6: R6.Pin_1, LED.green_anode
  N7: LED.common_cathode, Arduino1.GND, R8.Pin_0, R9.Pin_0, R10.Pin_0
  N8: Arduino1.A0, R7.pin_0, R10.Pin_1
  N9: Arduino1.A1, R9.Pin_1, R11.pin_0
  N10: Arduino1.A2, R8.Pin_1, R12.pin_0
  N11: Arduino1.5V, R7.pin_1, R11.pin_1, R12.pin_1
