# Fritzing sketch DIY_Capacitive_Piano (saved by Fritzing 0.8.7b)
breadboards: 1

parts:
  Part1 = Arduino Uno (Rev3)
  R1 = Resistor [tolerance=±5% resistance=1M package=THT]
  R2 = Resistor [tolerance=±5% resistance=1M package=THT]
  R3 = Resistor [tolerance=±5% resistance=1M package=THT]
  R4 = Resistor [tolerance=±5% resistance=1M package=THT]
  R5 = Resistor [tolerance=±5% resistance=1M package=THT]
  R6 = Resistor [tolerance=±5% resistance=1M package=THT]
  R7 = Resistor [tolerance=±5% resistance=1M package=THT]
  J1 = Piezo Speaker

nets:
  N1: Part1.D8, R6.Pin_0
  N2: Part1.D9_PWM, R7.Pin_0
  N3: Part1.D11_PWM/MOSI, J1.pin2
  N4: Part1.GND, J1.pin1
  N5: Part1.D2, R1.Pin_1, R2.Pin_1, R3.Pin_1, R4.Pin_1, R5.Pin_1, R6.Pin_1, R7.Pin_1
  N6: Part1.D3_PWM, R1.Pin_0
  N7: Part1.D4, R2.Pin_0
  N8: Part1.D5_PWM, R3.Pin_0
  N9: Part1.D6_PWM, R4.Pin_0
  N10: Part1.D7, R5.Pin_0

notes:
  PIANO
