# Fritzing sketch Knock_Arduino_example (saved by Fritzing 0.8.7b)
breadboards: 1

parts:
  Part1 = Arduino Uno (Rev3)
  J1 = Piezo Speaker
  R1 = Resistor [tolerance=±5% resistance=1M package=THT]

nets:
  N1: Part1.A0, J1.pin2, R1.Pin_0
  N2: Part1.GND, J1.pin1, R1.Pin_1
